// Logisim project MpMp25.circ as structural Verilog: 5 circuits, main circuit main
module main (
  input  RST
);

  wire clock_1_out, undriven;
  wire [7:0] alu_1_result, register_1_q, rf_1_data_out0, rf_1_data_out1, rf_1_pc;
  wire [15:0] controlled_buffer_1_out, rom_1_data;

  Clock clock_1 (.out(clock_1_out));
  CU cu_1 (.CLK(clock_1_out), .RST(RST), .Instruction(controlled_buffer_1_out));
  ROM #(.dataWidth(16)) rom_1 (.addr(rf_1_pc), .data(rom_1_data));
  RF rf_1 (
    .Data_In(rf_1_data_out0), .CLK(clock_1_out), .RST(RST), .Data_OUT0(rf_1_data_out0),
    .Data_OUT1(rf_1_data_out1), .PC(rf_1_pc));  // open: Addr0, Addr1, R_nW, CE0, CE1
  ALU alu_1 (.Op0(rf_1_data_out0), .Op1(rf_1_data_out1), .Result(alu_1_result));  // open: Flag_In, CMD_15_12, Flag_Out
  assign controlled_buffer_1_out = undriven ? rom_1_data : 16'bz;  // Controlled_Buffer controlled_buffer_1
  Controlled_Buffer #(.width(8)) controlled_buffer_2 (.in(register_1_q), .out(rf_1_data_out0));  // open: en
  Register register_1 (.D(alu_1_result), .Q(register_1_q));  // open: en, clk, clr

  // Notes on the sheet:
  //   Instruction bus
  //   Data bus
  //   hier steht Programmspeicher drin
  //   CE
  //   CE
endmodule

module ALU (
  input  [7:0] Op0,
  input  [7:0] Op1,
  input  [3:0] CMD_15_12,
  input  [7:0] Flag_In,
  output [7:0] Result,
  output [7:0] Flag_Out
);

  wire ADD_OFlag_Res, adder_1_cout, adder_2_cout, and_2_out, and_3_out, and_4_out, and_5_out,
       comparator_2_eq, comparator_3_eq, multiplexer_2_out, multiplexer_3_out, or_2_out, R, SUB_OFlag_Res,
       subtractor_1_bout, subtractor_2_bout, Z_out;
  wire [3:0] undriven_3;
  wire [7:0] adder_1_out, adder_2_out, and_1_out, divider_1_out, divider_1_rem, Flag_Select_data,
       multiplier_1_out, negator_1_out, not_1_out, or_1_out, shifter_1_out, shifter_2_out, subtractor_1_out,
       subtractor_2_out, undriven, undriven_2, undriven_4, xnor_1_out, xor_1_out;
  wire [8:0] shifter_3_out, shifter_4_out;

  // Probe on Op0
  // Probe on Op0
  // Probe on Op1
  // Probe on Op1
  ROM #(.addrWidth(4)) Flag_Select (.addr(CMD_15_12), .data(Flag_Select_data));
  Adder adder_1 (.a(Op0), .b(Op1), .out(adder_1_out), .cout(adder_1_cout));  // open: cin
  Subtractor subtractor_1 (.a(Op1), .b(Op0), .out(subtractor_1_out), .bout(subtractor_1_bout));  // open: bin
  Multiplier multiplier_1 (.a(Op0), .b(Op1), .out(multiplier_1_out));  // open: cin, cout
  Divider divider_1 (.a(Op1), .b(Op0), .out(divider_1_out), .upper({8{1'b0}}), .rem(divider_1_rem));
  Shifter shifter_1 (.in(Op0), .\dist (Op1[2:0]), .out(shifter_1_out));
  Shifter #(.shift("lr")) shifter_2 (.in(Op0), .\dist (Op1[2:0]), .out(shifter_2_out));
  Negator negator_1 (.in(Op0), .out(negator_1_out));
  assign and_1_out = Op0 & Op1;  // AND_Gate and_1, 8 bits wide
  assign or_1_out = Op0 | Op1;  // OR_Gate or_1, 8 bits wide
  assign xor_1_out = Op0 ^ Op1;  // XOR_Gate xor_1, 8 bits wide
  assign xnor_1_out = ~(Op0 ^ Op1);  // XNOR_Gate xnor_1, 8 bits wide
  assign not_1_out = ~Op0;  // NOT_Gate not_1, 8 bits wide
  Adder adder_2 (.a(Op1), .b(Op0), .out(adder_2_out), .cin(Flag_In[1]), .cout(adder_2_cout));
  Subtractor subtractor_2 (.a(Op1), .b(Op0), .out(subtractor_2_out), .bin(Flag_In[1]), .bout(subtractor_2_bout));
  Comparator comparator_1 (.a({8{1'b0}}), .b(divider_1_rem), .gt(R));  // open: eq, lt
  Comparator #(.width(4)) comparator_2 (.a(CMD_15_12), .b(4'b0001), .eq(comparator_2_eq));  // open: gt, lt
  or or_2 (or_2_out, comparator_2_eq, comparator_3_eq);
  Comparator #(.width(4)) comparator_3 (.a(CMD_15_12), .b(4'b1111), .eq(comparator_3_eq));  // open: gt, lt
  Multiplexer #(.select(4), .width(8)) multiplexer_1 (
    .in0(adder_1_out), .in1(subtractor_1_out), .in2(multiplier_1_out), .in3(divider_1_out),
    .in4(shifter_1_out), .in5(shifter_2_out), .in6(negator_1_out), .in7(undriven), .in8(undriven_2),
    .in9(and_1_out), .in10(or_1_out), .in11(xor_1_out), .in12(xnor_1_out), .in13(not_1_out),
    .in14(adder_2_out), .in15(subtractor_2_out), .out(Result), .sel(CMD_15_12));
  Multiplexer #(.select(4)) multiplexer_2 (
    .in0(adder_1_cout), .in1(subtractor_1_bout), .in14(adder_2_cout), .in15(subtractor_2_bout),
    .out(multiplexer_2_out), .sel(CMD_15_12));  // open: in2, in3, in4, in5, in6, in7, in8, in9, in10, in11, in12, in13
  // Probe on Result
  Multiplexer multiplexer_3 (.in0(ADD_OFlag_Res), .in1(SUB_OFlag_Res), .out(multiplexer_3_out), .sel(or_2_out));
  Multiplexer multiplexer_4 (.in0(Flag_In[0]), .in1(Z_out), .out(Flag_Out[0]), .sel(Flag_Select_data[0]));
  Multiplexer multiplexer_5 (.in0(Flag_In[1]), .in1(multiplexer_2_out), .out(Flag_Out[1]), .sel(Flag_Select_data[1]));
  Multiplexer multiplexer_6 (.in0(Flag_In[2]), .in1(multiplexer_3_out), .out(Flag_Out[2]), .sel(Flag_Select_data[2]));
  Multiplexer multiplexer_7 (.in0(Flag_In[3]), .out(Flag_Out[3]), .sel(Flag_Select_data[3]));  // open: in1
  Multiplexer multiplexer_8 (.in0(Flag_In[4]), .in1(R), .out(Flag_Out[4]), .sel(Flag_Select_data[4]));
  nor Z (Z_out, Result[0], Result[1], Result[2], Result[3], Result[4], Result[5], Result[6], Result[7]);
  // Probe on Op0
  // Probe on Op1
  // Probe on Result
  and and_2 (and_2_out, ~Op0[7], ~Op1[7], Result[7]);  // AND_Gate
  and and_3 (and_3_out, Op0[7], Op1[7], ~Result[7]);  // AND_Gate
  and and_4 (and_4_out, Op0[7], ~Op1[7], ~Result[7]);  // AND_Gate
  and and_5 (and_5_out, ~Op0[7], Op1[7], Result[7]);  // AND_Gate
  Shifter #(.width(9)) shifter_3 (.in({undriven_4, Flag_In[1]}), .\dist (undriven_3), .out(shifter_3_out));
  Shifter #(.shift("lr"), .width(9)) shifter_4 (.in({Flag_In[1], undriven_4}), .out(shifter_4_out));  // open: dist
  or or_3 (ADD_OFlag_Res, and_2_out, and_3_out);
  or or_4 (SUB_OFlag_Res, and_4_out, and_5_out);

  assign Flag_Out[7:5] = Flag_In[7:5];

  // Other names for the same wires on the sheet: C = Flag_In[1]; Op0_Tunnel[7:0] = Op0; Op1_Tunnel[7:0] = Op1

  // Notes on the sheet:
  //   ADD 0, SUB 1, ADDC 14; SUBC 15
  //   ADD 0x00, SUB 0x01, ADDC 0x0E; SUBC 0x0F
  //   +-
  //   +-
  //   contents of Flag_Select (hex, n*v repeats v):
  //   7 7 7 1 3 3 8*1 7 7
  //   Op1 kommt immer zuerst; guck in Git!
  //   nicht benutzte an Flag_In
  //     XXX,overflow_O, carry_C, zero_Z
  //   C_Flag
  //   O_Flag
  //   Z_Flag
  //   C_Flag
  //   O_Flag
  //   E_Flag
  //   R_Flag
  //   Shift mit Carry
  //   O_Flag ADD
  //   O_Flag SUB
  //   C_Flag Mux
  //   --> vielleicht mit xor
  //   Result Mux
endmodule

module CU (
  input  CLK,
  input  RST,
  input  [15:0] Instruction
);

  wire [1:0] Cyclecounter_q;
  wire [15:0] register_1_q;
  wire [31:0] rom_1_data;

  Register #(.width(16)) register_1 (.D(Instruction), .clk(CLK), .Q(register_1_q), .clr(RST));  // open: en
  Counter #(.max('h3), .width(2)) Cyclecounter (
    .Q(Cyclecounter_q), .clk(CLK), .clr(RST));  // open: load, D, count, carry, up
  ROM #(.addrWidth(9), .dataWidth(32)) rom_1 (
    .addr({register_1_q[7], register_1_q[11], register_1_q[6], register_1_q[15:12], Cyclecounter_q}),
    .data(rom_1_data));

  // Notes on the sheet:
  //   IMOPb[7]
  //   IMOPa[11]
  //   CMD[6]
  //   CMD0[15...12]
endmodule

module RF (
  input  [2:0] Addr0,
  input  [2:0] Addr1,
  input  [7:0] Data_In,
  input  R_nW,
  input  CE0,
  input  CE1,
  input  CLK,
  input  RST,
  output [7:0] Data_OUT0,
  output [7:0] Data_OUT1,
  output [7:0] PC
);

  wire decoder_1_out0, decoder_1_out1, not_1_out;
  wire [7:0] register_2_q;

  not not_1 (not_1_out, R_nW);
  Decoder #(.select(3)) decoder_1 (
    .out0(decoder_1_out0), .out1(decoder_1_out1), .sel(Addr0), .en(not_1_out));  // open: out2, out3, out4, out5, out6, out7
  Register register_1 (.D(Data_In), .en(decoder_1_out0), .Q(PC), .clk(CLK), .clr(RST));
  Register register_2 (.D(Data_In), .en(decoder_1_out1), .Q(register_2_q), .clk(CLK), .clr(RST));
  Register register_3 (.clk(CLK), .clr(RST));  // open: D, en, Q
  Register register_4 (.clk(CLK), .clr(RST));  // open: D, en, Q
  Register register_5 (.clk(CLK), .clr(RST));  // open: D, en, Q
  Register register_6 (.clk(CLK), .clr(RST));  // open: D, en, Q
  Register register_7 (.clk(CLK), .clr(RST));  // open: D, en, Q
  Register register_8 (.clk(CLK), .clr(RST));  // open: D, en, Q
  Multiplexer #(.disabled("Z"), .enable("true"), .select(3), .width(8)) multiplexer_1 (
    .in0(PC), .in1(register_2_q), .out(Data_OUT0), .sel(Addr0), .en(CE0));  // open: in2, in3, in4, in5, in6, in7
  Multiplexer #(.disabled("Z"), .enable("true"), .select(3), .width(8)) multiplexer_2 (
    .in0(PC), .in1(register_2_q), .out(Data_OUT1), .sel(Addr1), .en(CE1));  // open: in2, in3, in4, in5, in6, in7

  // Notes on the sheet:
  //   Registerfile
  //   speicher in dem register sind 
  //   Speicherdecoder wann geschrieben wird
  //   Read notWrite
  //   Chipenable
endmodule

module test_ALU (
);

  wire and_1_out, and_2_out, clock_1_out, comparator_1_eq, comparator_2_eq;
  wire [3:0] ALU_Command_data;
  wire [7:0] alu_1_flag_out, alu_1_result, Flag_result_data, Flags_In_data, Op0_data, Op1_data, Result_data;
  wire [9:0] Adresse;

  Clock clock_1 (.out(clock_1_out));
  Hex_Digit_Display hex_digit_display_1 (.value({2'b00, Adresse[9:8]}));  // open: dp
  Hex_Digit_Display hex_digit_display_2 (.value(Adresse[7:4]));  // open: dp
  and and_1 (and_1_out, clock_1_out, and_2_out);
  Hex_Digit_Display hex_digit_display_3 (.value(Adresse[3:0]));  // open: dp
  Counter #(.max('h3ff), .trigger("falling"), .width(10)) counter_1 (
    .Q(Adresse), .clk(and_1_out));  // open: load, D, count, carry, up, clr
  ROM #(.addrWidth(10), .dataWidth(4)) ALU_Command (.addr(Adresse), .data(ALU_Command_data));
  ROM #(.addrWidth(10)) Op0 (.addr(Adresse), .data(Op0_data));
  ROM #(.addrWidth(10)) Op1 (.addr(Adresse), .data(Op1_data));
  ROM #(.addrWidth(10)) Result (.addr(Adresse), .data(Result_data));
  ALU alu_1 (
    .Flag_In(Flags_In_data), .Op0(Op0_data), .Op1(Op1_data), .Result(alu_1_result), .Flag_Out(alu_1_flag_out));  // open: CMD_15_12
  Comparator comparator_1 (.a(alu_1_result), .b(Result_data), .eq(comparator_1_eq));  // open: gt, lt
  ROM #(.addrWidth(10)) Flags_In (.addr(Adresse), .data(Flags_In_data));
  ROM #(.addrWidth(10)) Flag_result (.addr(Adresse), .data(Flag_result_data));
  Comparator comparator_2 (.a(Flag_result_data), .b(alu_1_flag_out), .eq(comparator_2_eq));  // open: gt, lt
  LED led_1 (.in(and_2_out));
  and and_2 (and_2_out, comparator_2_eq, comparator_1_eq);

  // Notes on the sheet:
  //   contents of Op0 (hex, n*v repeats v):
  //   1 2 3 aa ff
  //   contents of Op1 (hex, n*v repeats v):
  //   4 5 6 57 1
  //   contents of Result (hex, n*v repeats v):
  //   5 7 9 1
  //   CMD15_12
  //   Op1
  //   Result
  //   Op0
  //   Flag_In
  //   Flag_Out
  //   contents of Flag_result (hex, n*v repeats v):
  //   0 0 0 2 3
endmodule
